// Logisim project alu.circ as structural Verilog: 10 circuits, main circuit main
module main (
  input  [2:0] opcode,
  input  [7:0] x,
  input  [7:0] y,
  output [7:0] \output ,
  output SF,
  output ZF,
  output CF,
  output OF,
  output EQ
);

  selector selector_1 (.x(x), .y(y), .opcode(opcode), .CF(CF), .\output (\output ), .ZF(ZF), .SF(SF), .EQ(EQ), .OF(OF));

  // Notes on the sheet:
  //   CS 31 Lab 3, Part 2: ALU
  //   Ghazi and Gidon
endmodule

module ADD_010 (
  input  [7:0] x,
  input  [7:0] y,
  input  [2:0] opcode,
  output [7:0] \output ,
  output out_5
);

  wire adder_1_cout, comparator_1_eq;
  wire [7:0] adder_1_out;

  Adder adder_1 (.a(x), .b(y), .out(adder_1_out), .cout(adder_1_cout));  // open: cin
  assign \output  = comparator_1_eq ? adder_1_out : 8'bz;  // Controlled_Buffer controlled_buffer_1
  assign out_5 = comparator_1_eq ? adder_1_cout : 1'bz;  // Controlled_Buffer controlled_buffer_2
  Comparator #(.width(3)) comparator_1 (.a(opcode), .b(3'b010), .eq(comparator_1_eq));  // open: gt, lt
endmodule

module OR_000 (
  input  [7:0] x,
  input  [7:0] y,
  input  [2:0] opcode,
  output [7:0] \output 
);

  wire comparator_1_eq;
  wire [7:0] or_out;

  assign or_out = x | y;  // OR_Gate or, 8 bits wide
  Comparator #(.width(3)) comparator_1 (.a(opcode), .b(3'b000), .eq(comparator_1_eq));  // open: gt, lt
  assign \output  = comparator_1_eq ? or_out : 8'bz;  // Controlled_Buffer controlled_buffer_1
endmodule

module AND_001 (
  input  [7:0] x,
  input  [7:0] y,
  input  [2:0] opcode,
  output [7:0] \output 
);

  wire comparator_1_eq;
  wire [7:0] and_out;

  assign and_out = x & y;  // AND_Gate and, 8 bits wide
  Comparator #(.width(3)) comparator_1 (.a(opcode), .b(3'b001), .eq(comparator_1_eq));  // open: gt, lt
  assign \output  = comparator_1_eq ? and_out : 8'bz;  // Controlled_Buffer controlled_buffer_1
endmodule

module SUB_011 (
  input  [7:0] x,
  input  [7:0] y,
  input  [2:0] opcode,
  output [7:0] \output ,
  output out_5
);

  wire adder_2_cout, comparator_1_eq;
  wire [7:0] adder_1_out, adder_2_out, bit_extender_1_out, bit_flipper_out;

  assign bit_extender_1_out = {{7{1'b0}}, 1'b1};  // Bit_Extender bit_extender_1
  assign bit_flipper_out = ~y;  // NOT_Gate bit_flipper, 8 bits wide
  Adder adder_1 (.a(bit_flipper_out), .b(bit_extender_1_out), .out(adder_1_out));  // open: cin, cout
  assign out_5 = comparator_1_eq ? adder_2_cout : 1'bz;  // Controlled_Buffer controlled_buffer_1
  Adder adder_2 (.a(x), .b(adder_1_out), .out(adder_2_out), .cout(adder_2_cout));  // open: cin
  assign \output  = comparator_1_eq ? adder_2_out : 8'bz;  // Controlled_Buffer controlled_buffer_2
  Comparator #(.width(3)) comparator_1 (.a(opcode), .b(3'b011), .eq(comparator_1_eq));  // open: gt, lt
endmodule

module leftLogicalShift_100 (
  input  [7:0] x,
  input  [7:0] y,
  input  [2:0] opcode,
  output [7:0] \output 
);

  wire comparator_1_eq;
  wire [7:0] shifter_1_out;

  Shifter shifter_1 (.in(x), .\dist (y[2:0]), .out(shifter_1_out));
  assign \output  = comparator_1_eq ? shifter_1_out : 8'bz;  // Controlled_Buffer controlled_buffer_1
  Comparator #(.width(3)) comparator_1 (.a(opcode), .b(3'b100), .eq(comparator_1_eq));  // open: gt, lt
endmodule

module rightLogicalShift_101 (
  input  [7:0] x,
  input  [7:0] y,
  input  [2:0] opcode,
  output [7:0] \output 
);

  wire comparator_1_eq;
  wire [7:0] shifter_1_out;

  Shifter #(.shift("lr")) shifter_1 (.in(x), .\dist (y[2:0]), .out(shifter_1_out));
  assign \output  = comparator_1_eq ? shifter_1_out : 8'bz;  // Controlled_Buffer controlled_buffer_1
  Comparator #(.width(3)) comparator_1 (.a(opcode), .b(3'b101), .eq(comparator_1_eq));  // open: gt, lt
endmodule

module rightArithmeticShift_110 (
  input  [7:0] x,
  input  [7:0] y,
  input  [2:0] opcode,
  output [7:0] \output 
);

  wire comparator_1_eq;
  wire [7:0] shifter_1_out;

  Shifter #(.shift("ar")) shifter_1 (.in(x), .\dist (y[2:0]), .out(shifter_1_out));
  assign \output  = comparator_1_eq ? shifter_1_out : 8'bz;  // Controlled_Buffer controlled_buffer_1
  Comparator #(.width(3)) comparator_1 (.a(opcode), .b(3'b110), .eq(comparator_1_eq));  // open: gt, lt
endmodule

module comparator_111 (
  input  [7:0] x,
  input  [7:0] y,
  input  [2:0] opcode,
  output [7:0] out_4
);

  wire comparator_1_lt, comparator_2_eq;
  wire [7:0] bit_extender_1_out;

  Comparator comparator_1 (.a(x), .b(y), .lt(comparator_1_lt));  // open: gt, eq
  assign out_4 = comparator_2_eq ? bit_extender_1_out : 8'bz;  // Controlled_Buffer controlled_buffer_1
  assign bit_extender_1_out = {{7{1'b0}}, comparator_1_lt};  // Bit_Extender bit_extender_1
  Comparator #(.width(3)) comparator_2 (.a(opcode), .b(3'b111), .eq(comparator_2_eq));  // open: gt, lt
endmodule

module selector (
  input  [7:0] x,
  input  [7:0] y,
  input  [2:0] opcode,
  output CF,
  output [7:0] \output ,
  output ZF,
  output SF,
  output EQ,
  output OF
);

  wire ADD_out_5, comparator_1_eq, comparator_3_eq, comparator_7_eq, comparator_8_eq, not_1_out, not_2_out,
       not_3_out, or_2_out;

  Comparator #(.width(1)) comparator_1 (.a(y[7]), .b(x[7]), .eq(comparator_1_eq));  // open: gt, lt
  not not_1 (not_1_out, comparator_1_eq);
  ADD_010 ADD (.x(x), .y(y), .opcode(opcode), .out_5(ADD_out_5), .\output (\output ));
  OR_000 OR (.x(x), .y(y), .opcode(opcode), .\output (\output ));
  AND_001 AND (.x(x), .y(y), .opcode(opcode), .\output (\output ));
  SUB_011 SUB (.x(x), .y(y), .opcode(opcode), .out_5(ADD_out_5), .\output (\output ));
  leftLogicalShift_100 LLS (.x(x), .y(y), .opcode(opcode), .\output (\output ));
  rightLogicalShift_101 RLS (.x(x), .y(y), .opcode(opcode), .\output (\output ));
  rightArithmeticShift_110 RAS (.x(x), .y(y), .opcode(opcode), .\output (\output ));
  comparator_111 COMP (.x(x), .y(y), .opcode(opcode), .out_4(\output ));
  Comparator comparator_2 (.a(x), .b(y), .eq(EQ));  // open: gt, lt
  assign OF = not_1_out ? comparator_1_eq : 1'bz;  // Controlled_Buffer controlled_buffer_1
  Comparator #(.width(1)) comparator_3 (.a(\output [7]), .b(x[7]), .eq(comparator_3_eq));  // open: gt, lt
  not not_2 (not_2_out, comparator_3_eq);
  assign OF = comparator_1_eq ? not_2_out : 1'bz;  // Controlled_Buffer controlled_buffer_2
  Comparator comparator_4 (.a(\output ), .b({8{1'b0}}), .eq(ZF));  // open: gt, lt
  Comparator #(.width(1)) comparator_5 (.a(ADD_out_5), .b(1'b0), .lt(CF));  // open: gt, eq
  assign CF = not_3_out ? 1'b0 : 1'bz;  // Controlled_Buffer controlled_buffer_3
  Comparator #(.width(1)) comparator_6 (.a(\output [7]), .b(1'b1), .eq(SF));  // open: gt, lt
  Comparator #(.width(3)) comparator_7 (.a(opcode), .b(3'b010), .eq(comparator_7_eq));  // open: gt, lt
  Comparator #(.width(3)) comparator_8 (.a(opcode), .b(3'b011), .eq(comparator_8_eq));  // open: gt, lt
  or or_2 (or_2_out, comparator_7_eq, comparator_8_eq);
  not not_3 (not_3_out, or_2_out);
endmodule
