// Logisim project part1.circ as structural Verilog: 4 circuits, main circuit main
module main (
  input  [3:0] Ghazi___Gidon,
  input  [1:0] y,
  input  carry_in,
  output [3:0] sum,
  output carry_out
);

  wire [3:0] signext2to4_1__4bit_out;

  signext2to4 signext2to4_1 (._2bit_in(y), ._4bit_out(signext2to4_1__4bit_out));
  fulladder4 fulladder4_1 (
    .x(Ghazi___Gidon), .y(signext2to4_1__4bit_out), .carry_in(carry_in), .sum(sum), .carry_out(carry_out));

  // Notes on the sheet:
  //   CS 31 Lab 3, Part 1
  //   x
  //   signext2to4
  //   fulladder
endmodule

module signext2to4 (
  input  [1:0] _2bit_in,
  output [3:0] _4bit_out
);


  assign _4bit_out = {{3{_2bit_in[1]}}, _2bit_in[0]};
endmodule

module fulladder (
  input  x,
  input  y,
  input  carry_in,
  output sum,
  output carry_out
);

  wire and_1_out, and_2_out, xor_1_out;

  xor xor_1 (xor_1_out, x, y);
  and and_1 (and_1_out, x, y);
  xor xor_2 (sum, xor_1_out, carry_in);
  and and_2 (and_2_out, xor_1_out, carry_in);
  or or_1 (carry_out, and_2_out, and_1_out);
endmodule

module fulladder4 (
  input  [3:0] x,
  input  [3:0] y,
  input  carry_in,
  output [3:0] sum,
  output carry_out
);

  wire fulladder_1_carry_out, fulladder_2_carry_out, fulladder_3_carry_out;

  fulladder fulladder_1 (.x(x[0]), .y(y[0]), .carry_in(carry_in), .sum(sum[0]), .carry_out(fulladder_1_carry_out));
  fulladder fulladder_2 (
    .x(x[1]), .y(y[1]), .carry_in(fulladder_1_carry_out), .sum(sum[1]), .carry_out(fulladder_2_carry_out));
  fulladder fulladder_3 (
    .x(x[2]), .y(y[2]), .carry_in(fulladder_2_carry_out), .sum(sum[2]), .carry_out(fulladder_3_carry_out));
  fulladder fulladder_4 (.x(x[3]), .y(y[3]), .carry_in(fulladder_3_carry_out), .sum(sum[3]), .carry_out(carry_out));

  // Notes on the sheet:
  //   adder0
  //   1 bit
  //   adder1
  //   adder2
  //   1 bit
  //   1 bit
  //   adder3
  //   1 bit
endmodule
